# Fritzing sketch Protoboard (saved by Fritzing 0.8.7b)
breadboards: 1

parts:
  Componente1 = Arduino Uno (Rev3)
  LCD1 = LCD screen
  R1 = Rotary Potentiometer (Small) [maximum_resistance=10kΩ package=THT]
  LED1 = RGB LED (com. anode, rbg) [package="5 mm [THT]"]
  R2 = Photocell (LDR) [package=THT]
  R3 = Photocell (LDR) [package=THT]
  R4 = Photocell (LDR) [package=THT]
  R5 = Photocell (LDR) [package=THT]
  R6 = Photocell (LDR) [package=THT]
  R7 = Photocell (LDR) [package=THT]
  LED2 = LED - 5mm [color="White (8000K)" package="5 mm [THT]"]
  LED3 = LED - 5mm [color="White (8000K)" package="5 mm [THT]"]
  J1 = Piezo Speaker
  R8 = Resistor [tolerance=±5% resistance=100 package=THT]

nets:
  N1: Componente1.A0, R3.pin_1
  N2: Componente1.A1, R4.pin_1
  N3: Componente1.A2, R5.pin_1
  N4: Componente1.A3, R6.pin_1
  N5: Componente1.A4/SDA, R7.pin_1
  N6: Componente1.A5/SCL, R2.pin_1
  N7: Componente1.D10_PWM/SS, LCD1.E
  N8: Componente1.D11_PWM/MOSI, LCD1.RS
  N9: Componente1.D0/RX, LED1.red_cathode
  N10: Componente1.D1/TX, LED1.blue_cathode
  N11: Componente1.D2, LED1.green_cathode
  N12: Componente1.D3_PWM, LCD1.DB7
  N13: Componente1.D4, LCD1.DB6
  N14: Componente1.D5_PWM, LCD1.DB5
  N15: Componente1.D6_PWM, LCD1.DB4
  N16: Componente1.D7, R8.Pin_1
  5V: Componente1.5V, LCD1.VDD, LCD1.LED+, R1.leg1, LED2.cathode, LED3.cathode
  GND: Componente1.GND, LCD1.VSS, LCD1.R/W, LCD1.LED-, R1.leg2, LED1.common_anode, R2.pin_0, R3.pin_0, R4.pin_0, R5.pin_0, R6.pin_0, R7.pin_0, LED2.anode, LED3.anode, J1.pin1
  N17: LCD1.V0, R1.wiper
  N18: J1.pin2, R8.Pin_0
